# Fritzing sketch DeviceSchematic (saved by Fritzing 0.9.6b)
breadboards: 1

parts:
  U1 = ESP32S-HiLetgo [part_number=ESP32S-HiLetgo]
  Chirp!_Soil_Moisture_Sensor1 = Chirp! Soil Moisture Sensor v2.7.3
  DHT1 = DHT11 Humitidy and Temperature Sensor
  Mod1 = KY-018 Photoresistor Module [package="Breakout board"]

nets:
  N1: U1.GPIO39, Chirp!_Soil_Moisture_Sensor1.pin_3
  N2: U1.GPIO34, Mod1.S
  VDD: U1.GPIO6, Chirp!_Soil_Moisture_Sensor1.Pin_1, DHT1.VDD, Mod1.Vin
  N3: U1.GPIO7, Chirp!_Soil_Moisture_Sensor1.pin_5, DHT1.GND, Mod1.-
  N4: U1.GPIO2, DHT1.DATA

custom parts:
  ESP32S-HiLetgo: HiLetgo ESP-WROOM-32 ESP32 ESP-32S Development Board 2.4GHz Dual-Mode WiFi + Bluetooth Dual Cores Microcontroller The ESP32 integrated with Antenna switches, RF Balun, power amplifiers, low-noise amplifiers, filters, and management modules, and the entire solution occupies the least area of PCB. 2.4 GHz Wi-Fi plus Bluetooth dual-mode chip, with TSMC Ultra-low power consumption 40nm technology,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
  DHT11 Humitidy and Temperature Sensor: DHT11 Humidity and Temperature Sensor
  KY-018 Photoresistor Module: KY-018 Photoresistor module, used to measure light intensity. It can determine the presence or absence of light.
